// Digital circuit CPU.dig as structural Verilog
module CPU (
  input  Clk,
  output [7:0] AC,
  output [7:0] MQ
);

  wire DQ, DQ_t;
  wire [2:0] Sir;
  wire [7:0] driver_1_out, N_d, Op_d, QN, Sac, SN, Sn_t;
  wire [7:3] IR_q;

  EEPROM #(.AddrBits(8), .Bits(8)) Op (.A(QN), .CS(1'b1), .WE(1'b0), .OE(1'b1), .D(Op_d));
  EEPROM #(.AddrBits(8), .Bits(8)) N (.A(QN), .CS(1'b1), .WE(1'b0), .OE(1'b1), .D(N_d));
  Register #(.Bits(8)) PCN (.D(SN), .C(DQ_t), .en(1'b1), .Q(QN));
  assign driver_1_out = DQ ? Op_d : 8'bz;  // Driver driver_1
  assign driver_1_out = DQ_t ? N_d : 8'bz;  // Driver driver_2
  // somador_8bits somador_8bits_1: pin names not known; wires that end beside it: QN, 8'h1, 1'b0, SN
  Register #(.Bits(8)) IR (.D(driver_1_out), .C(Clk), .en(DQ), .Q({IR_q, Sir}));
  Register #(.Bits(8)) N_2 (.D(driver_1_out), .C(Clk), .en(DQ_t), .Q(Sn_t));
  Register #(.Bits(8)) u_AC (.D(AC), .C(Clk), .en(DQ), .Q(Sac));
  seletor seletor_1 (.OP(Sir), .A(Sac), .B(Sn_t), .Clock(Clk), .Enbl(DQ_t), .AC(AC), .MQ(MQ));
  D_FF d_ff_1 (.D(DQ_t), .C(Clk), .Q(DQ), .nQ(DQ_t));

  // Other names for the same wires on the sheet: QALU[7:0] = AC

  // Notes on the sheet:
  //   contents of Op (hex, n*v repeats v):
  //   0,1,2,3,4,5,6,7
  //   contents of N (hex, n*v repeats v):
  //   5,3,2,3,1,4,6,1,1,2,2,3,2,4,2,2
endmodule
