// Digital circuit contador.dig as structural Verilog
module contador (
  input  clk,
  output [7:0] out_2
);

  wire [7:0] S;

  Register #(.Bits(8)) PC (.D(S), .C(clk), .en(1'b1), .Q(out_2));
  Seven_Seg_Hex seven_seg_hex_1 (.d(out_2[3:0]), .dp(1'b0));
  // somador_8bits somador_8bits_1: pin names not known; wires that end beside it: out_2, 8'h1, 1'b0, S

  // Other names for the same wires on the sheet: Q[7:0] = out_2
endmodule
