// Digital circuit seletor.dig as structural Verilog
module seletor (
  input  [2:0] OP,
  input  [7:0] A,
  input  [7:0] B,
  input  Clock,
  input  Enbl,
  output [7:0] AC,
  output [7:0] MQ
);

  wire [7:0] AND, MQ_t, Mult, R, S, S7, Shift_Left, Shift_Right, Soma, Sub, W, XOR;

  // somador_8bits somador_8bits_1: pin names not known; wires that end beside it: A, B, 1'b0, Soma
  Multiplexer #(.Selector_Bits(3), .Bits(8)) multiplexer_1 (
    .sel(OP), .in_0(Soma), .in_1(Sub), .in_2(Shift_Right), .in_3(Shift_Left), .in_4(AND), .in_5(XOR),
    .in_6(Mult), .in_7(R), .out(S));
  Multiplexer #(.Selector_Bits(3), .Bits(8)) multiplexer_2 (
    .sel(OP), .in_0({8{1'b0}}), .in_1({8{1'b0}}), .in_2({8{1'b0}}), .in_3({8{1'b0}}), .in_4({8{1'b0}}),
    .in_5({8{1'b0}}), .in_6(W), .in_7(S7), .out(MQ_t));
  // subtrator_8bits subtrator_8bits_1: pin names not known; wires that end beside it: A, B, 1'b1, Sub
  // AND8bits and8bits_1: pin names not known; wires that end beside it: A, B, AND
  Mul #(.Bits(8)) mul_1 (.a(A), .b(B), .mul({W, Mult}));
  Register #(.Bits(8)) u_AC (.D(S), .C(Clock), .en(Enbl), .Q(AC));
  Register #(.Bits(8)) u_MQ (.D(MQ_t), .C(Clock), .en(Enbl), .Q(MQ));
  // shift_right shift_right_1: pin names not known; wires that end beside it: A, Shift_Right
  // XOR8bits xor8bits_1: pin names not known; wires that end beside it: A, B, XOR
  Div #(.Bits(8)) div_1 (.a(A), .b(B), .q(S7), .r(R));
  // shift_left shift_left_1: pin names not known; wires that end beside it: A, Shift_Left

  // Notes on the sheet:
  //   OP	Operação
  //   000	soma - 0
  //   001	sub - 1
  //   010	Shift Right - 2
  //   011	Shift Left - 3
  //   100	AND - 4 
  //   101	XOR - 5
  //   110                    MUlT - 6
  //   111                    DIV - 7
endmodule
